# Fritzing sketch FritzingSketch (saved by Fritzing 0.9.3b)

parts:
  Part1 = Arduino Mega ADK (Rev3)
  J1 = shrouded pin header, 10 pins [form="♂ (shrouded male)"]
  J2 = shrouded pin header, 10 pins [form="♂ (shrouded male)"]
  J3 = shrouded pin header, 10 pins [form="♂ (shrouded male)"]  # not connected
  U3 = atmega168 [package=dip]
  IC1 = 4060 [package="DIP16 [THT]"]
  IC2 = 4060 [package="DIP16 [THT]"]  # not connected
  J4 = shrouded pin header, 10 pins [form="♂ (shrouded male)"]
  R1 = PHOTOCELL [package=photocell-kit]
  RHT1 = Humidity and Temperature Sensor RHT03
  Part2 = NRF24L01
  U4 = atmega168 [package=dip]
  U5 = RELAY [package=relay-jzc]  # not connected
  R2 = Resistor [tolerance=±5% resistance=10k package="0402 [SMD]"]

nets:
  N1: Part1.A6, R1.P$2, R2.Pin_0
  N2: Part1.A7, IC1.Q13
  N3: Part1.D13_PWM, Part2.SCK
  N4: Part1.D12_PWM, Part2.MISO
  N5: Part1.D11_PWM, Part2.MOSI
  N6: Part1.D10_PWM, Part2.CSN
  N7: Part1.D9_PWM, Part2.CE
  3V3: Part1.3V3, Part2.VCC
  5V: Part1.5V, U3.RESET, R1.P$1, RHT1.Vcc
  GND: Part1.GND, U3.D6_(PWM), U3.A4, IC1.Q3, IC1.GND, RHT1.GND_1, Part2.GND, U4.D6_(PWM), U4.A4, R2.Pin_1
  N8: Part1.D22, U3.D8
  N9: Part1.D23, U3.D9_(PWM)
  N10: Part1.D24, U3.D10_(PWM)
  N11: Part1.D25, U3.D11_(PWM)
  N12: Part1.D26, U4.RESET
  N13: Part1.D28, U4.D8
  N14: Part1.D29, U4.D9_(PWM)
  N15: Part1.D30, U4.D10_(PWM)
  N16: Part1.D31, U4.D11_(PWM)
  N17: Part1.D34, IC1.VDD
  N18: Part1.D36, IC1.RS
  N19: Part1.D37, IC1.REXT
  N20: Part1.D38, IC1.CEXT
  N21: Part1.D48, RHT1.Data-signal
  N22: J1.pin1, U3.D5_(PWM)
  N23: J1.pin2, U3.A1
  N24: J1.pin3, U3.GND
  N25: J1.pin4, U3.AVCC
  N26: J1.pin5, U3.D12
  N27: J1.pin6, U3.D13
  N28: J1.pin7, U3.AREF
  N29: J1.pin8, U3.A0
  N30: J1.pin9, U3.A2
  N31: J1.pin10, U3.XLAT2
  N32: J2.pin1, U4.D5_(PWM)
  N33: J2.pin2, U4.A1
  N34: J2.pin3, U4.GND
  N35: J2.pin4, U4.AVCC
  N36: J2.pin5, U4.D12
  N37: J2.pin6, U4.D13
  N38: J2.pin7, U4.AREF
  N39: J2.pin8, U4.A0
  N40: J2.pin9, U4.A2
  N41: J2.pin10, U4.XLAT2
  N42: IC1.Q11, J4.pin3
  N43: IC1.Q12, J4.pin4
  N44: IC1.Q5, J4.pin7
  N45: IC1.Q4, J4.pin8
  N46: IC1.MR, J4.pin2
  N47: IC1.Q8, J4.pin10
  N48: IC1.Q7, J4.pin1
  N49: IC1.Q9, J4.pin9

notes:
  4501
  https://playground.arduino.cc/Learning/4051
  DG406
  photoresistor
  http://www.instructables.com/id/How-to-use-a-photoresistor-or-photocell-Arduino-Tu/
  Humidity temp http://www.circuitbasics.com/how-to-set-up-the-dht11-humidity-sensor-on-an-arduino/
  NRF24l01+
